# Fritzing sketch ESP8266_Gardening (saved by Fritzing 0.9.3b)
breadboards: 1

parts:
  U1 = NodeMCU V1.0
  Part1 = Soil Moisture Sensor
  KY-2 = Keyes Relay [package=THT]
  R1 = Resistor [tolerance=±5% resistance=220 package=THT]

nets:
  3V3: U1.3V3, Part1.VCC, R1.Pin_0
  GND: U1.GND, Part1.GND, KY-2.ground
  N1: U1.D5, KY-2.signal
  N2: U1.Vin, KY-2.power
  N3: U1.A0, Part1.SIG, R1.Pin_1

custom parts:
  NodeMCU V1.0: ESP8266 based NodeMCU
  Keyes Relay: The Keyes 5V relay module is suitable for SCM development, home appliance control. It uses a 5V~12V TIL control signal which can control DC / AC signal.
